// Logisim project reptile-8.circ as structural Verilog
module D_Latch (
  input  D,
  input  clk,
  input  clr,
  output Q
);

  wire nand_1_out, nand_2_out, nand_4_out, nor_1_out, not_1_out, not_2_out;

  not not_1 (not_1_out, D);
  nand nand_1 (nand_1_out, D, clk);
  nand nand_2 (nand_2_out, clk, not_1_out);
  not not_2 (not_2_out, nand_2_out);
  nor nor_1 (nor_1_out, not_2_out, clr);
  nand nand_3 (Q, nand_1_out, nand_4_out);
  nand nand_4 (nand_4_out, Q, nor_1_out);

  // Notes on the sheet:
  //   clk: pull=down
  //   clr: pull=down
  //   D: pull=down
  //   Q: pull=down
endmodule

module D_Flip_Flop (
  input  D,
  input  write,
  input  clk,
  output Q
);

  wire d_latch_1_q, multiplexer_1_out, not_1_out;

  Multiplexer #(.enable("false")) multiplexer_1 (.in0(Q), .in1(D), .out(multiplexer_1_out), .sel(write));
  not not_1 (not_1_out, clk);
  D_Latch d_latch_1 (.D(multiplexer_1_out), .clk(not_1_out), .clr(1'b0), .Q(d_latch_1_q));
  D_Latch d_latch_2 (.D(d_latch_1_q), .clk(clk), .clr(1'b0), .Q(Q));

  // Notes on the sheet:
  //   write: pull=down
  //   D: pull=down
  //   Q: pull=down
  //   clk: pull=down
endmodule

module ALU_1 (
  input  op1,
  input  op2,
  input  cin,
  input  [2:0] s,
  output cout,
  output out
);

  wire and_1_out, and_2_out, and_3_out, not_1_out, or_1_out, xor_1_out, xor_2_out, xor_3_out;

  xor xor_1 (xor_1_out, op1, op2);
  and and_1 (and_1_out, xor_1_out, cin);
  and and_2 (and_2_out, op2, op1);
  and and_3 (and_3_out, op1, op2);
  or or_1 (or_1_out, op1, op2);
  not not_1 (not_1_out, op1);
  xor xor_2 (xor_2_out, xor_1_out, cin);
  xor xor_3 (xor_3_out, op1, op2);
  or or_2 (cout, and_1_out, and_2_out);
  Multiplexer #(.select(3), .enable("false")) multiplexer_1 (
    .in0(xor_2_out), .in1(and_3_out), .in2(or_1_out), .in3(xor_3_out), .in4(not_1_out), .in5(op1), .out(out),
    .sel(s));  // open: in6, in7
endmodule

module ALU (
  input  [15:0] op1,
  input  [15:0] op2,
  input  [3:0] s,
  output [15:0] out
);

  wire alu_1_1_cout, alu_1_2_cout, alu_1_3_cout, alu_1_4_cout, alu_1_5_cout, alu_1_6_cout, alu_1_7_cout,
       alu_1_8_cout, alu_1_9_cout, alu_1_10_cout, alu_1_11_cout, alu_1_12_cout, alu_1_13_cout, alu_1_14_cout,
       alu_1_15_cout, and_1_out, and_2_out, and_3_out, and_4_out, and_5_out, and_6_out, and_7_out, and_8_out,
       and_9_out, and_10_out, not_1_out, not_2_out, not_3_out, not_4_out, not_5_out, not_6_out, not_7_out,
       not_8_out, not_9_out, not_10_out, not_11_out, not_12_out, not_13_out;
  wire [1:0] or_5_out;
  wire [2:0] or_1_out;
  wire [15:0] multiplexer_1_out, not_14_out;

  not not_1 (not_1_out, s[0]);
  not not_2 (not_2_out, s[1]);
  not not_3 (not_3_out, s[0]);
  not not_4 (not_4_out, s[3]);
  not not_5 (not_5_out, s[3]);
  not not_6 (not_6_out, s[1]);
  not not_7 (not_7_out, s[2]);
  not not_8 (not_8_out, s[0]);
  not not_9 (not_9_out, s[2]);
  not not_10 (not_10_out, s[1]);
  not not_11 (not_11_out, s[2]);
  not not_12 (not_12_out, s[3]);
  not not_13 (not_13_out, s[2]);
  and and_1 (and_1_out, ~s[3], ~s[2], ~s[1], s[0]);  // AND_Gate
  and and_2 (and_2_out, not_1_out, not_2_out, s[3]);
  and and_3 (and_3_out, not_3_out, s[1], not_4_out);
  and and_4 (and_4_out, s[0], s[1], not_5_out);
  and and_5 (and_5_out, not_6_out, s[3]);
  and and_6 (and_6_out, s[0], s[2]);
  and and_7 (and_7_out, s[3], s[1], not_7_out, not_8_out);
  and and_8 (and_8_out, s[3], s[1], s[0], not_9_out);
  and and_9 (and_9_out, s[0], not_10_out, not_11_out, not_12_out);
  and and_10 (and_10_out, s[0], s[1], s[3], not_13_out);
  or or_1 (or_1_out[0], and_2_out, s[2], and_3_out);
  or or_2 (or_1_out[1], s[2], and_4_out);
  or or_3 (or_1_out[2], and_5_out, and_6_out);
  or or_4 (or_5_out[1], and_7_out, and_8_out);
  or or_5 (or_5_out[0], and_9_out, and_10_out);
  assign not_14_out = ~op2;  // NOT_Gate not_14, 16 bits wide
  Multiplexer #(.select(2), .width(16), .enable("false")) multiplexer_1 (
    .in0(op2), .in1(not_14_out), .in2(16'h1), .in3({16{1'b1}}), .out(multiplexer_1_out), .sel(or_5_out));
  ALU_1 alu_1_1 (
    .op1(op1[0]), .op2(multiplexer_1_out[0]), .cin(and_1_out), .cout(alu_1_1_cout), .out(out[0]), .s(or_1_out));
  ALU_1 alu_1_2 (
    .op1(op1[1]), .op2(multiplexer_1_out[1]), .cin(alu_1_1_cout), .cout(alu_1_2_cout), .out(out[1]),
    .s(or_1_out));
  ALU_1 alu_1_3 (
    .op1(op1[2]), .op2(multiplexer_1_out[2]), .cin(alu_1_2_cout), .cout(alu_1_3_cout), .out(out[2]),
    .s(or_1_out));
  ALU_1 alu_1_4 (
    .op1(op1[3]), .op2(multiplexer_1_out[3]), .cin(alu_1_3_cout), .cout(alu_1_4_cout), .out(out[3]),
    .s(or_1_out));
  ALU_1 alu_1_5 (
    .op1(op1[4]), .op2(multiplexer_1_out[4]), .cin(alu_1_4_cout), .cout(alu_1_5_cout), .out(out[4]),
    .s(or_1_out));
  ALU_1 alu_1_6 (
    .op1(op1[5]), .op2(multiplexer_1_out[5]), .cin(alu_1_5_cout), .cout(alu_1_6_cout), .out(out[5]),
    .s(or_1_out));
  ALU_1 alu_1_7 (
    .op1(op1[6]), .op2(multiplexer_1_out[6]), .cin(alu_1_6_cout), .cout(alu_1_7_cout), .out(out[6]),
    .s(or_1_out));
  ALU_1 alu_1_8 (
    .op1(op1[7]), .op2(multiplexer_1_out[7]), .cin(alu_1_7_cout), .cout(alu_1_8_cout), .out(out[7]),
    .s(or_1_out));
  ALU_1 alu_1_9 (
    .op1(op1[8]), .op2(multiplexer_1_out[8]), .cin(alu_1_8_cout), .cout(alu_1_9_cout), .out(out[8]),
    .s(or_1_out));
  ALU_1 alu_1_10 (
    .op1(op1[9]), .op2(multiplexer_1_out[9]), .cin(alu_1_9_cout), .cout(alu_1_10_cout), .out(out[9]),
    .s(or_1_out));
  ALU_1 alu_1_11 (
    .op1(op1[10]), .op2(multiplexer_1_out[10]), .cin(alu_1_10_cout), .cout(alu_1_11_cout), .out(out[10]),
    .s(or_1_out));
  ALU_1 alu_1_12 (
    .op1(op1[11]), .op2(multiplexer_1_out[11]), .cin(alu_1_11_cout), .cout(alu_1_12_cout), .out(out[11]),
    .s(or_1_out));
  ALU_1 alu_1_13 (
    .op1(op1[12]), .op2(multiplexer_1_out[12]), .cin(alu_1_12_cout), .cout(alu_1_13_cout), .out(out[12]),
    .s(or_1_out));
  ALU_1 alu_1_14 (
    .op1(op1[13]), .op2(multiplexer_1_out[13]), .cin(alu_1_13_cout), .cout(alu_1_14_cout), .out(out[13]),
    .s(or_1_out));
  ALU_1 alu_1_15 (
    .op1(op1[14]), .op2(multiplexer_1_out[14]), .cin(alu_1_14_cout), .cout(alu_1_15_cout), .out(out[14]),
    .s(or_1_out));
  ALU_1 alu_1_16 (
    .op1(op1[15]), .op2(multiplexer_1_out[15]), .cin(alu_1_15_cout), .out(out[15]), .s(or_1_out));  // open: cout
endmodule
